// Logisim project e2468726.circ as structural Verilog: 2 circuits, main circuit main
module main (
  input  A1,
  input  A0,
  input  B1,
  input  B0,
  input  O2,
  input  O1,
  input  O0,
  output L3,
  output L2,
  output L1,
  output L0
);

  wire and_1_out, and_2_out, and_3_out, and_4_out, and_5_out, and_6_out, and_7_out,
       n3_to_8_decoder_74138_1_p2, n3_to_8_decoder_74138_1_p4, n3_to_8_decoder_74138_1_p6,
       n3_to_8_decoder_74138_1_p7, n4_to_1_mux_x2_74153_1_p11, n4_to_1_mux_x2_74153_1_p13,
       n4_to_1_mux_x2_74153_1_p14, n4_to_1_mux_x2_74153_2_p11, n4_to_1_mux_x2_74153_2_p12,
       n4_to_1_mux_x2_74153_3_p8, n4_to_1_mux_x2_74153_3_p10, n4_to_1_mux_x2_74153_3_p11, nor_1_out,
       nor_2_out, not_1_out, not_3_out, or_1_out, or_2_out, or_4_out, or_5_out, xor_1_out, xor_2_out,
       xor_3_out, xor_4_out, xor_5_out;

  not not_1 (not_1_out, A0);
  and and_1 (and_1_out, not_1_out, B0);
  and and_2 (and_2_out, A0, B0);
  // _4_to_1_MUX__x2___74153 #(.Facing("east")) 4_to_1_mux_x2_74153_1: pin names not known; wires that end beside it: 1'b1, 1'b1, B0, 1'b1, 1'b0, 1'b1, 1'b0, B0, A1, B1, n4_to_1_mux_x2_74153_1_p11, A0, n4_to_1_mux_x2_74153_1_p13, n4_to_1_mux_x2_74153_1_p14
  xor xor_1 (xor_1_out, B0, A0);
  xor xor_2 (xor_2_out, B1, A1);
  and and_3 (and_3_out, B0, A0);
  and and_4 (and_4_out, B1, A1);
  nor nor_1 (nor_1_out, B0, A0);
  nor nor_2 (nor_2_out, B1, A1);
  xor xor_3 (xor_3_out, B0, A0);
  and and_5 (and_5_out, B0, A0);
  xor xor_4 (xor_4_out, B1, A1);
  and and_6 (and_6_out, B1, A1);
  or or_1 (or_1_out, and_2_out, B1);
  not not_2 (n4_to_1_mux_x2_74153_1_p11, A1);
  xor xor_5 (xor_5_out, xor_4_out, and_5_out);
  and and_7 (and_7_out, and_5_out, xor_4_out);
  or or_2 (or_2_out, n4_to_1_mux_x2_74153_1_p13, n4_to_1_mux_x2_74153_1_p14);
  // OR_Gate or_3 has open pins: in0=and_7_out, in1=and_6_out, out=open
  not not_3 (not_3_out, O2);
  // _4_to_1_MUX__x2___74153 #(.Facing("east")) 4_to_1_mux_x2_74153_2: pin names not known; wires that end beside it: xor_3_out, and_1_out, or_2_out, xor_1_out, and_3_out, nor_1_out, O2, O0, not_3_out, O1, n4_to_1_mux_x2_74153_2_p11, n4_to_1_mux_x2_74153_2_p12
  or or_4 (or_4_out, n4_to_1_mux_x2_74153_2_p12, n4_to_1_mux_x2_74153_2_p11);
  // _4_to_1_MUX__x2___74153 #(.Facing("east")) 4_to_1_mux_x2_74153_3: pin names not known; wires that end beside it: xor_5_out, or_1_out, xor_2_out, and_4_out, nor_2_out, O2, O0, n4_to_1_mux_x2_74153_3_p8, O1, n4_to_1_mux_x2_74153_3_p10, n4_to_1_mux_x2_74153_3_p11
  not not_4 (n4_to_1_mux_x2_74153_3_p8, O2);
  or or_5 (or_5_out, n4_to_1_mux_x2_74153_3_p11, n4_to_1_mux_x2_74153_3_p10);
  // _3_to_8_decoder__74138 #(.Facing("south")) 3_to_8_decoder_74138_1: pin names not known; wires that end beside it: or_4_out, n3_to_8_decoder_74138_1_p2, or_5_out, n3_to_8_decoder_74138_1_p4, 1'b0, n3_to_8_decoder_74138_1_p6, n3_to_8_decoder_74138_1_p7, 1'b1, 1'b0, 1'b0
  not not_5 (L3, n3_to_8_decoder_74138_1_p7);
  not not_6 (L2, n3_to_8_decoder_74138_1_p6);
  not not_7 (L1, n3_to_8_decoder_74138_1_p4);
  not not_8 (L0, n3_to_8_decoder_74138_1_p2);

  // Notes on the sheet:
  //   A_0'
  //   O_0
  //   B_0
  //   A_0
  //   B_0
  //   B_1
  //   B_1
  //   !!!-Careful-!!!
  //   A_0
  //   B_0
  //   O_0
  //   A_0
  //   XOR
  //   B_1
  //   O_1
  //   A_1
  //   B_0
  //   O_0
  //   A_0
  //   AND
  //   B_1
  //   O_1
  //   A_1
  //   B_0
  //   O_0
  //   A_0
  //   NOR
  //   B_1
  //   O_1
  //   A_1
  //   O_0
  //   CARRY_0
  //   O_1
  //   B>=A
  //   O_1
  //   O_0
  //   CARRY_1
  //   Won't be used
  //   O_0
  //   S
  //   X
  //   S
  //   X
  //   X
  //   O_1
endmodule

module Full_Adder (
  input  I_0,
  input  I_1,
  input  C_in,
  output S,
  output C_out
);

  wire and_1_out, and_2_out, xor_1_out;

  xor xor_1 (xor_1_out, I_0, I_1);
  xor xor_2 (S, xor_1_out, C_in);
  and and_1 (and_1_out, xor_1_out, C_in);
  and and_2 (and_2_out, I_0, I_1);
  or or_1 (C_out, and_1_out, and_2_out);
endmodule
