// Logisim project e2468726.circ as structural Verilog: 2 circuits, main circuit main
module main (
  input  A1,
  input  A0,
  input  B1,
  input  B0,
  input  O2,
  input  O1,
  input  O0,
  output L6,
  output L5,
  output L4,
  output L3,
  output L2,
  output L1,
  output L0,
  output S
);

  wire and_1_out, and_2_out, and_3_out, and_4_out, and_5_out, and_6_out, and_7_out, and_8_out, and_10_out,
       and_11_out, and_12_out, and_13_out, and_14_out, and_15_out, and_16_out, and_17_out, and_18_out,
       and_19_out, n3_to_8_decoder_74138_1_p2, n3_to_8_decoder_74138_1_p4, n3_to_8_decoder_74138_1_p6,
       n3_to_8_decoder_74138_1_p7, n3_to_8_decoder_74138_1_p8, n3_to_8_decoder_74138_1_p9,
       n3_to_8_decoder_74138_1_p10, n4_to_1_mux_x2_74153_1_p2, n4_to_1_mux_x2_74153_1_p4,
       n4_to_1_mux_x2_74153_1_p9, n4_to_1_mux_x2_74153_2_p5, n4_to_1_mux_x2_74153_2_p7,
       n4_to_1_mux_x2_74153_2_p8, n4_to_1_mux_x2_74153_3_p11, n4_to_1_mux_x2_74153_3_p12,
       n4_to_1_mux_x2_74153_4_p12, n4_to_1_mux_x2_74153_4_p13, nor_1_out, nor_2_out, not_1_out, not_2_out,
       not_3_out, not_4_out, not_5_out, not_6_out, not_7_out, or_1_out, or_2_out, or_4_out, or_5_out,
       or_7_out, or_8_out, or_9_out, or_10_out, xor_1_out, xor_2_out, xor_3_out, xor_4_out, xor_5_out,
       xor_6_out, xor_7_out, xor_8_out, xor_9_out, xor_10_out, xor_11_out, xor_12_out;

  not not_1 (not_1_out, A1);
  not not_2 (not_2_out, A0);
  not not_3 (not_3_out, B1);
  not not_4 (not_4_out, B0);
  and and_1 (and_1_out, A0, B1);
  and and_2 (and_2_out, A1, B0);
  and and_3 (and_3_out, not_2_out, B1);
  and and_4 (and_4_out, A0, B0);
  and and_5 (and_5_out, not_1_out, not_2_out);
  and and_6 (and_6_out, B0, A0);
  and and_7 (and_7_out, B1, A1);
  xor xor_1 (xor_1_out, A0, O0);
  xor xor_2 (xor_2_out, A1, O0);
  xor xor_3 (xor_3_out, 1'b0, O0);
  or or_1 (or_1_out, and_1_out, and_2_out);
  or or_2 (or_2_out, and_3_out, and_4_out);
  and and_8 (and_8_out, and_5_out, B0);
  // _4_to_1_MUX__x2___74153 #(.Facing("east")) 4_to_1_mux_x2_74153_1: pin names not known; wires that end beside it: 1'b1, n4_to_1_mux_x2_74153_1_p2, B1, n4_to_1_mux_x2_74153_1_p4, 1'b0, A0, 1'b0, A1, n4_to_1_mux_x2_74153_1_p9
  or or_3 (n4_to_1_mux_x2_74153_1_p2, B0, B1);
  and and_9 (n4_to_1_mux_x2_74153_1_p4, B1, B0);
  xor xor_4 (xor_4_out, B0, A0);
  xor xor_5 (xor_5_out, B1, A1);
  nor nor_1 (nor_1_out, B0, A0);
  nor nor_2 (nor_2_out, B1, A1);
  xor xor_6 (xor_6_out, B0, xor_1_out);
  xor xor_7 (xor_7_out, B1, xor_2_out);
  xor xor_8 (xor_8_out, 1'b0, xor_3_out);
  xor xor_9 (xor_9_out, xor_6_out, O0);
  and and_10 (and_10_out, O0, xor_6_out);
  and and_11 (and_11_out, B0, xor_1_out);
  xor xor_10 (xor_10_out, xor_7_out, or_4_out);
  and and_12 (and_12_out, or_4_out, xor_7_out);
  and and_13 (and_13_out, B1, xor_2_out);
  xor xor_11 (xor_11_out, xor_8_out, or_5_out);
  and and_14 (and_14_out, or_5_out, xor_8_out);
  and and_15 (and_15_out, 1'b0, xor_3_out);
  or or_4 (or_4_out, and_10_out, and_11_out);
  or or_5 (or_5_out, and_12_out, and_13_out);
  // OR_Gate or_6 has open pins: in0=and_14_out, in1=and_15_out, out=open
  and and_16 (and_16_out, O0, xor_11_out);
  and and_17 (and_17_out, xor_11_out, xor_12_out);
  not not_5 (not_5_out, xor_11_out);
  and and_18 (and_18_out, xor_10_out, not_5_out);
  not not_6 (not_6_out, O2);
  not not_7 (not_7_out, O1);
  and and_19 (and_19_out, not_6_out, not_7_out);
  and and_20 (S, and_16_out, and_19_out);
  or or_7 (or_7_out, and_18_out, and_17_out);
  xor xor_12 (xor_12_out, xor_9_out, xor_10_out);
  // _4_to_1_MUX__x2___74153 #(.Facing("east")) 4_to_1_mux_x2_74153_2: pin names not known; wires that end beside it: xor_11_out, or_1_out, O2, O0, n4_to_1_mux_x2_74153_2_p5, O1, n4_to_1_mux_x2_74153_2_p7, n4_to_1_mux_x2_74153_2_p8
  // _4_to_1_MUX__x2___74153 #(.Facing("east")) 4_to_1_mux_x2_74153_3: pin names not known; wires that end beside it: xor_10_out, or_7_out, or_2_out, xor_5_out, and_7_out, nor_2_out, O2, O0, n4_to_1_mux_x2_74153_2_p5, O1, n4_to_1_mux_x2_74153_3_p11, n4_to_1_mux_x2_74153_3_p12
  // _4_to_1_MUX__x2___74153 #(.Facing("east")) 4_to_1_mux_x2_74153_4: pin names not known; wires that end beside it: xor_9_out, xor_9_out, and_8_out, n4_to_1_mux_x2_74153_1_p9, xor_4_out, and_6_out, nor_1_out, O2, O0, n4_to_1_mux_x2_74153_2_p5, O1, n4_to_1_mux_x2_74153_4_p12, n4_to_1_mux_x2_74153_4_p13
  or or_8 (or_8_out, n4_to_1_mux_x2_74153_2_p7, n4_to_1_mux_x2_74153_2_p8);
  or or_9 (or_9_out, n4_to_1_mux_x2_74153_3_p11, n4_to_1_mux_x2_74153_3_p12);
  or or_10 (or_10_out, n4_to_1_mux_x2_74153_4_p12, n4_to_1_mux_x2_74153_4_p13);
  // _3_to_8_decoder__74138 #(.Facing("south")) 3_to_8_decoder_74138_1: pin names not known; wires that end beside it: or_10_out, n3_to_8_decoder_74138_1_p2, or_9_out, n3_to_8_decoder_74138_1_p4, or_8_out, n3_to_8_decoder_74138_1_p6, n3_to_8_decoder_74138_1_p7, n3_to_8_decoder_74138_1_p8, n3_to_8_decoder_74138_1_p9, n3_to_8_decoder_74138_1_p10, 1'b1, 1'b0, 1'b0
  not not_8 (n4_to_1_mux_x2_74153_2_p5, O2);
  not not_9 (L6, n3_to_8_decoder_74138_1_p10);
  not not_10 (L5, n3_to_8_decoder_74138_1_p9);
  not not_11 (L4, n3_to_8_decoder_74138_1_p8);
  not not_12 (L3, n3_to_8_decoder_74138_1_p7);
  not not_13 (L2, n3_to_8_decoder_74138_1_p6);
  not not_14 (L1, n3_to_8_decoder_74138_1_p4);
  not not_15 (L0, n3_to_8_decoder_74138_1_p2);

  // Notes on the sheet:
  //   A0
  //   B1
  //   A1
  //   B0
  //   A0'
  //   B1
  //   A0
  //   B0
  //   A1'
  //   A0'
  //   B0
  //   AND
  //   O_0
  //   XOR
  //   O_1
  //   O_0
  //   O_1
  //   O_0
  //   NOR
  //   O_1
  //   B>=A
  //   SUM/SUB_0
  //   CARRY_0
  //   SUM/SUB_1
  //   CARRY_1
  //   SUM/SUB_2
  //   CARRY_2
  //   GENERAL OTUPUT 2
  //   GENERAL OTUPUT 1
  //   GENERAL OTUPUT 0
endmodule

module Full_Adder (
  input  I_0,
  input  I_1,
  input  C_in,
  output S,
  output C_out
);

  wire and_1_out, and_2_out, xor_1_out;

  xor xor_1 (xor_1_out, I_0, I_1);
  xor xor_2 (S, xor_1_out, C_in);
  and and_1 (and_1_out, xor_1_out, C_in);
  and and_2 (and_2_out, I_0, I_1);
  or or_1 (C_out, and_1_out, and_2_out);
endmodule
